# Fritzing sketch RC522s_with_Uno (saved by Fritzing 0.9.3b)
breadboards: 1

parts:
  Part1 = Arduino Uno (Rev3)
  Part2 = RFID-RC522-v2
  Part3 = RFID-RC522-v2
  Part4 = RFID-RC522-v2

nets:
  N1: Part1.D8, Part4.SDA
  N2: Part1.D9_PWM, Part1.D11_PWM/MOSI, Part1.D12/MISO, Part1.D13/SCK, Part2.SCK, Part2.MOSI, Part2.MISO, Part3.SDA, Part3.SCK, Part3.MOSI, Part3.MISO, Part4.SCK, Part4.MOSI, Part4.MISO
  N3: Part1.D10_PWM/SS, Part2.SDA
  3.3V: Part1.3V3, Part2.3.3V, Part3.RST, Part3.3.3V, Part4.3.3V
  GND: Part1.GND, Part2.GND, Part3.GND, Part4.GND

custom parts:
  RFID-RC522-v2: A simple China made RFID-RC522 Reader; do check the pin labels, as this is a MFRC522 based clone.

// code stored in the sketch: RC522_readers_for_fritzing.ino
#include <SPI.h>
#include <MFRC522.h>

////////////// wiring
#define RST_PIN         3          // Not connected to modules, only configured
// connect to SDA of the modules
#define SS_PIN_1        10
#define SS_PIN_2        9
#define SS_PIN_3        8
#define SS_PIN_4        7
//  pin   connect_to
//  11    MOSI
//  12    MISO
//  13    SCK

// total amount of modules
#define NR_OF_READERS   4

// SDA pin array
byte ssPins[] = {SS_PIN_1, SS_PIN_2, SS_PIN_3, SS_PIN_4};

// reader instances
MFRC522 mfrc522[NR_OF_READERS];

/**
   Initialize.
*/
void setup() {

  Serial.begin(9600); // Initialize serial communications with the PC
  while (!Serial);    // Do nothing if no serial port is opened (added for Arduinos based on ATMEGA32U4)

  SPI.begin();        // Init SPI bus

  for (uint8_t reader = 0; reader < NR_OF_READERS; reader++) {
    mfrc522[reader].PCD_Init(ssPins[reader], RST_PIN); // Init each MFRC522 card
    Serial.print(F("Reader "));
    Serial.print(reader);
    Serial.print(F(": "));
    mfrc522[reader].PCD_DumpVersionToSerial();
  }
}

/**
   Main loop.
*/
void loop() {

  for (uint8_t reader = 0; reader < NR_OF_READERS; reader++) {
    // Look for new cards

    if (mfrc522[reader].PICC_IsNewCardPresent() && mfrc522[reader].PICC_ReadCardSerial()) {
      Serial.print(F("Reader "));
      Serial.print(reader);
      // Show some details of the PICC (that is: the tag/card)
      Serial.print(F(": Card UID:"));
      dump_byte_array(mfrc522[reader].uid.uidByte, mfrc522[reader].uid.size);
      Serial.println();
      Serial.print(F("PICC type: "));
      MFRC522::PICC_Type piccType = mfrc522[reader].PICC_GetType(mfrc522[reader].uid.sak);
      Serial.println(mfrc522[reader].PICC_GetTypeName(piccType));

      // Halt PICC
      mfrc522[reader].PICC_HaltA();
      // Stop encryption on PCD
      mfrc522[reader].PCD_StopCrypto1();
    } //if (mfrc522[reader].PICC_IsNewC
  } //for(uint8_t reader
}

/**
   Helper routine to dump a byte array as hex values to Serial.
*/
void dump_byte_array(byte *buffer, byte bufferSize) {
  for (byte i = 0; i < bufferSize; i++) {
    Serial.print(buffer[i] < 0x10 ? " 0" : " ");
    Serial.print(buffer[i], HEX);
  }
}

// code stored in the sketch: RC522s_with_Uno.ino
#include <SPI.h>
#include <MFRC522.h>

////////////// wiring
#define RST_PIN         3          // Not connected to modules, only configured
// connect to SDA of the modules
#define SS_PIN_1        10
#define SS_PIN_2        9
#define SS_PIN_3        8
#define SS_PIN_4        7
//  pin   connect_to
//  11    MOSI
//  12    MISO
//  13    SCK

// total amount of modules
#define NR_OF_READERS   4

// SDA pin array
byte ssPins[] = {SS_PIN_1, SS_PIN_2, SS_PIN_3, SS_PIN_4};

// reader instances
MFRC522 mfrc522[NR_OF_READERS];

/**
   Initialize.
*/
void setup() {

  Serial.begin(9600); // Initialize serial communications with the PC
  while (!Serial);    // Do nothing if no serial port is opened (added for Arduinos based on ATMEGA32U4)

  SPI.begin();        // Init SPI bus

  for (uint8_t reader = 0; reader < NR_OF_READERS; reader++) {
    mfrc522[reader].PCD_Init(ssPins[reader], RST_PIN); // Init each MFRC522 card
    Serial.print(F("Reader "));
    Serial.print(reader);
    Serial.print(F(": "));
    mfrc522[reader].PCD_DumpVersionToSerial();
  }
}

/**
   Main loop.
*/
void loop() {

  for (uint8_t reader = 0; reader < NR_OF_READERS; reader++) {
    // Look for new cards

    if (mfrc522[reader].PICC_IsNewCardPresent() && mfrc522[reader].PICC_ReadCardSerial()) {
      Serial.print(F("Reader "));
      Serial.print(reader);
      // Show some details of the PICC (that is: the tag/card)
      Serial.print(F(": Card UID:"));
      dump_byte_array(mfrc522[reader].uid.uidByte, mfrc522[reader].uid.size);
      Serial.println();
      Serial.print(F("PICC type: "));
      MFRC522::PICC_Type piccType = mfrc522[reader].PICC_GetType(mfrc522[reader].uid.sak);
      Serial.println(mfrc522[reader].PICC_GetTypeName(piccType));

      // Halt PICC
      mfrc522[reader].PICC_HaltA();
      // Stop encryption on PCD
      mfrc522[reader].PCD_StopCrypto1();
    } //if (mfrc522[reader].PICC_IsNewC
  } //for(uint8_t reader
}

/**
   Helper routine to dump a byte array as hex values to Serial.
*/
void dump_byte_array(byte *buffer, byte bufferSize) {
  for (byte i = 0; i < bufferSize; i++) {
    Serial.print(buffer[i] < 0x10 ? " 0" : " ");
    Serial.print(buffer[i], HEX);
  }
}

// code stored in the sketch: ReadUidMultiReader.ino
#include <SPI.h>
#include <MFRC522.h>

////////////// wiring
#define RST_PIN         3          // Not connected to modules, only configured
// connect to SDA of the modules
#define SS_PIN_1        10
#define SS_PIN_2        9
#define SS_PIN_3        8
#define SS_PIN_4        7
//  pin   connect_to
//  11    MOSI
//  12    MISO
//  13    SCK

// total amount of modules
#define NR_OF_READERS   4

// SDA pin array
byte ssPins[] = {SS_PIN_1, SS_PIN_2, SS_PIN_3, SS_PIN_4};

// reader instances
MFRC522 mfrc522[NR_OF_READERS];

/**
   Initialize.
*/
void setup() {

  Serial.begin(9600); // Initialize serial communications with the PC
  while (!Serial);    // Do nothing if no serial port is opened (added for Arduinos based on ATMEGA32U4)

  SPI.begin();        // Init SPI bus

  for (uint8_t reader = 0; reader < NR_OF_READERS; reader++) {
    mfrc522[reader].PCD_Init(ssPins[reader], RST_PIN); // Init each MFRC522 card
    Serial.print(F("Reader "));
    Serial.print(reader);
    Serial.print(F(": "));
    mfrc522[reader].PCD_DumpVersionToSerial();
  }
}

/**
   Main loop.
*/
void loop() {

  for (uint8_t reader = 0; reader < NR_OF_READERS; reader++) {
    // Look for new cards

    if (mfrc522[reader].PICC_IsNewCardPresent() && mfrc522[reader].PICC_ReadCardSerial()) {
      Serial.print(F("Reader "));
      Serial.print(reader);
      // Show some details of the PICC (that is: the tag/card)
      Serial.print(F(": Card UID:"));
      dump_byte_array(mfrc522[reader].uid.uidByte, mfrc522[reader].uid.size);
      Serial.println();
      Serial.print(F("PICC type: "));
      MFRC522::PICC_Type piccType = mfrc522[reader].PICC_GetType(mfrc522[reader].uid.sak);
      Serial.println(mfrc522[reader].PICC_GetTypeName(piccType));

      // Halt PICC
      mfrc522[reader].PICC_HaltA();
      // Stop encryption on PCD
      mfrc522[reader].PCD_StopCrypto1();
    } //if (mfrc522[reader].PICC_IsNewC
  } //for(uint8_t reader
}

/**
   Helper routine to dump a byte array as hex values to Serial.
*/
void dump_byte_array(byte *buffer, byte bufferSize) {
  for (byte i = 0; i < bufferSize; i++) {
    Serial.print(buffer[i] < 0x10 ? " 0" : " ");
    Serial.print(buffer[i], HEX);
  }
}
